# Fritzing sketch Fritzing_prototype_sketch (saved by Fritzing 0.9.3b)
breadboards: 1

parts:
  U1 = NodeMCU V1.0
  U2 = RELAY [package=relay-jzc]
  Power_plug1 = Power plug
  U3 = RELAY [package=relay-jzc]
  Power_plug2 = Power plug
  U4 = RELAY [package=relay-jzc]
  U5 = RELAY [package=relay-jzc]
  Power_plug3 = Power plug
  Power_plug4 = Power plug
  U6 = ACS712 [package=so08]

nets:
  N1: U1.D0, U2.COIL1
  N2: U1.D1, U1.TX, U3.COIL1
  N3: U1.D2, U4.COIL1
  N4: U1.D3, U5.COIL1
  N5: U1.A0, U6.VOUT
  GND: U2.COIL2, U3.COIL2, U4.COIL2, U5.COIL2, U6.GND
  N6: U2.MAIN, Power_plug1.VCC
  N7: U3.MAIN, Power_plug2.VCC
  N8: U4.MAIN, Power_plug3.VCC
  N9: U5.MAIN, Power_plug4.VCC

custom parts:
  NodeMCU V1.0: ESP8266 based NodeMCU V1.0
